# Fritzing sketch FritzingThrustTest (saved by Fritzing 0.9.2b)
breadboards: 1

parts:
  Part1 = HX711 Weighing Sensor Module
  U1 = STM32F303 [package=LQFP-48]
  Load_Cell1 = Load Cell - Red/white/black/green
  Part2 = FTDI Basic Programmer

nets:
  N1: Part1.VCC, U1.3V3#40
  N2: Part1.GND, U1.GNS
  N3: Part1.DO/RX, U1.A12
  N4: Part1.CK/TX, U1.A11
  N5: Part1.E+, Load_Cell1.wire1
  N6: Part1.E-, Load_Cell1.wire2
  N7: Part1.A+, Load_Cell1.wire3
  N8: Part1.A-, Load_Cell1.wire4
  N9: U1.A9, Part2.RXI
  N10: U1.A10, Part2.TXO

custom parts:
  STM32F303: Medium density Cortex-M3 microcontroller.
  Load Cell - Red/white/black/green: A rectangle load cell/weighting pressure Sensor with four wires - Red, white, black, green. Normally corresponding with E+, E-, A+, A- respectively.
